# Fritzing sketch Arduino_Weather_Station (saved by Fritzing 0.9.3b)
breadboards: 1

parts:
  RHT1 = Humidity and Temperature Sensor RHT03
  LCD1 = LCD screen
  Εξάρτημα1 = Arduino Uno (Rev3)
  R1 = Resistor [tolerance=±5% resistance=4.7k package=THT]
  R2 = Resistor [tolerance=±5% resistance=330 package=THT]
  R3 = Resistor [tolerance=±5% resistance=330 package=THT]
  R4 = Resistor [tolerance=±5% resistance=330 package=THT]
  LED1 = RGB LED - (4 legs) [package="5 mm [THT]"]  # not connected

nets:
  VCC: RHT1.Vcc, LCD1.VDD, LCD1.LED+, Εξάρτημα1.5V, R1.Pin_0
  N1: RHT1.Data-signal, Εξάρτημα1.D2, R1.Pin_1
  VSS: RHT1.GND_1, RHT1.GND_2, LCD1.VSS, LCD1.R/W, LCD1.LED-, Εξάρτημα1.GND
  N2: LCD1.RS, Εξάρτημα1.D8
  N3: LCD1.E, Εξάρτημα1.D9_PWM
  N4: LCD1.DB4, Εξάρτημα1.D4
  N5: LCD1.DB5, Εξάρτημα1.D5_PWM
  N6: LCD1.DB6, Εξάρτημα1.D6_PWM
  N7: LCD1.DB7, Εξάρτημα1.D7
  N8: Εξάρτημα1.D11_PWM/MOSI, R2.Pin_0
  N9: Εξάρτημα1.D12/MISO, R3.Pin_0
  N10: Εξάρτημα1.D13/SCK, R4.Pin_0

// code stored in the sketch: FullProgramm.ino
/*
Arduino 2x16 LCD - Detect Buttons
modified on 18 Feb 2019
by Saeed Hosseini @ Electropeak
https://electropeak.com/learn/
*/
#include <LiquidCrystal.h>
#include <dht.h>
dht DHT;
//Constants
#define DHT11_PIN 2
//LCD pin to Arduino
int redpin = 11;
int bluepin = 13;
int greenpin = 12;
const int pin_RS = 8; 
const int pin_EN = 9; 
const int pin_d4 = 4; 
const int pin_d5 = 5; 
const int pin_d6 = 6; 
const int pin_d7 = 7; 
const int pin_BL = 10; 
float hum;  //Stores humidity value
float tempc; //Stores temperature value
float tempf; //Stores temperature value
LiquidCrystal lcd( pin_RS,  pin_EN,  pin_d4,  pin_d5,  pin_d6,  pin_d7);
void setup() {
  pinMode(11,OUTPUT);
  pinMode(12,OUTPUT);
  pinMode(13,OUTPUT);
 Serial.begin(9600);
 lcd.begin(16, 2);
}
void loop() {
 

 int chk = DHT.read11(DHT11_PIN);
    //Read data and store it to variables hum and temp
    hum = DHT.humidity;
    tempc= DHT.temperature;
    tempf= (tempc*1.8)+32;
    //Print temp and humidity values to serial monitor    
    
    lcd.setCursor(0,0);
    lcd.print("Temp:");
    lcd.setCursor(0,1);
    lcd.print("Humi:");
    lcd.setCursor(6,0);
    lcd.print(tempc); 
    lcd.print(" C");  
    lcd.setCursor(6,1);
    lcd.print(hum);
    lcd.print(" %");
    if(tempc<19){
    digitalWrite(bluepin, LOW);
    digitalWrite(redpin, HIGH);
    digitalWrite(greenpin, HIGH);  
  }
  else if(tempc>22){
    digitalWrite(bluepin, HIGH);
    digitalWrite(redpin, LOW);
    digitalWrite(greenpin, HIGH);
  }
  else{
    digitalWrite(bluepin, HIGH);
    digitalWrite(redpin, HIGH);
    digitalWrite(greenpin, LOW);
  }
 
 
 int x;
 x = analogRead (0);
 if (x < 60) {
   lcd.clear();
   TempCheck(tempc);
   lcd.clear();
 }
 else if (x < 200) {    //up
    lcd.clear();
    lcd.setCursor(0,0);
    lcd.print("Temp:");
    lcd.setCursor(0,1);
    lcd.print("Humi:");
    lcd.setCursor(6,0);
    lcd.print(tempc); 
    lcd.print(" C");  
    lcd.setCursor(6,1);
    lcd.print(hum);
    lcd.print(" %");
    delay(2000);
    lcd.clear();
 }
 else if (x < 400){   //down
    lcd.clear();
    lcd.setCursor(0,0);
    lcd.print("Temp:");
    lcd.setCursor(0,1);
    lcd.print("Humi:");
    lcd.setCursor(6,0);
    lcd.print(tempf); 
    lcd.print(" F");
    lcd.setCursor(6,1);
    lcd.print(hum);
    lcd.print(" %");
    delay(2000);
    lcd.clear();
 }
 else if (x < 600){   //left
   lcd.clear();
   HumidityCheck(hum);
   lcd.clear();
 }
 else if (x < 800){//select
   lcd.clear();
   lcd.setCursor(0,0);
   lcd.print("Break!!!");
   goto BREAK;
 }

BREAK:

 delay(250);  
} 

//Humidity Check and Temp Check
void HumidityCheck(float humidity){
  if(humidity<30){
    lcd.setCursor(0,0);
    lcd.print("Dry Environment");
    delay(2000);
    }
  else if(humidity>=30&&humidity<=45){
    lcd.setCursor(0,0);
    lcd.print("Perfect Environment");
    delay(2000);
  }
  else{
    lcd.setCursor(0,0);
    lcd.print("Moist Environment");
    delay(2000);
  }
  }
void TempCheck(float temperature) {
if(temperature<19){
    lcd.setCursor(0,0);
    lcd.print("Cold Environment");
    delay(2000);
    }
  else if(temperature>=19&&temperature<=22){
    lcd.setCursor(0,0);
    lcd.print("Perfect Environment");
    delay(2000);
  }
  else{
    lcd.setCursor(0,0);
    lcd.print("Hot Environment");
    delay(2000);
  }
  }
